# Fritzing sketch Componentes (saved by Fritzing 0.9.3b)
breadboards: 2

parts:
  S1 = H-Bridge with L298N
  U1 = LCD-16X2 [package=lcd-16x2]
  hc-sr1 = hc-sr04
  F1 = Fan - Ventilador [package=THT]
  Componente1 = Arduino Mega 2560 (Rev3)
  VCC3 = Battery
  VCC4 = Battery
  VCC5 = Battery
  VCC6 = Battery
  R1 = TRIMPOT [package=3362u-2]
  R2 = Resistor [tolerance=±5% resistance=220 package=THT]
  F2 = Fan - Ventilador [package=THT]
  Componente2 = Bluetooth HC-05 Macho

nets:
  VCC: S1.12V, U1.VDD, hc-sr1.VCC, Componente1.5V, VCC4.+, R1.CW, R2.Pin_0, F2.5V, Componente2.VCC
  GND: S1.GND, U1.VSS, U1.R_W, U1.K, hc-sr1.GND, Componente1.GND, VCC5.-, R1.CCW, F2.GND, Componente2.GND
  5V: S1.5V, Componente1.VIN
  N1: S1.IN3, Componente1.D7_PWM
  N2: S1.IN4, Componente1.D6_PWM
  N3: S1.OUT3-Motor2, F1.GND
  N4: S1.OUT4-Motor2, F1.5V
  N5: U1.VO, R1.WIPER
  N6: U1.RS, Componente1.D13_PWM
  N7: U1.E, Componente1.D12_PWM
  N8: U1.DB4, Componente1.D11_PWM
  N9: U1.DB5, Componente1.D10_PWM
  N10: U1.DB6, Componente1.D9_PWM
  N11: U1.DB7, Componente1.D8_PWM
  N12: U1.A, R2.Pin_1
  N13: hc-sr1.Trig, Componente1.D4_PWM
  N14: hc-sr1.Echo, Componente1.D3_PWM
  N15: Componente1.D0_RX0, Componente2.TXD
  N16: Componente1.D1_TX0, Componente2.RXD
  N17: VCC3.-, VCC5.+
  N18: VCC3.+, VCC6.-
  N19: VCC4.-, VCC6.+

notes:
  Faltó pin 5D a ENB, para controlar velocidad
  Ventilador 12v que cambia de velocidad para posicionar el objeto en el punto requerido
  Bateria 12v
  Puente H
  Pantalla LCD 16 x 2
  Sensor Ultrasonico
  HC-SR04
  Arduino Mega 2560
  Ventilador 12v que impulsa aire debajo de la base del levitador
  Bluetooth conectado a los pines de transmición del arduino

custom parts:
  H-Bridge with L298N: h-bridge
  Fan - Ventilador: Ventilador de 2 pines, se encuentra comunmente en computadoras de escritorio
